// Logisim project ORT2Project.circ as structural Verilog: 8 circuits, main circuit COMPUTER
module COMPUTER (
);

  wire BTN_RST_out, CLK, cpu_1_inta, interrupt_interface_4_1_p4, interrupt_interface_4_1_p5,
       interrupt_interface_4_1_p6, interrupt_interface_4_1_p7, pull_resistor_4_node, pull_resistor_5_node,
       ram_1_out_8, rst;
  wire [1:0] cpu_1_uext1__0;
  wire [3:0] interrupt_interface_4_1_p1;
  wire [7:0] pull_resistor_2_node, ram_1_out_7;
  wire [15:0] pull_resistor_1_node;

  Button BTN_RST (.out(BTN_RST_out));
  Clock u_CLK (.out(CLK));
  // RisingEdge risingedge_1: pin names not known; wires that end beside it: BTN_RST_out, CLK, rst
  RAM ram_1 (
    .in_1(pull_resistor_1_node), .in_2(CLK), .in_3(pull_resistor_2_node), .in_4(pull_resistor_4_node),
    .in_5(pull_resistor_5_node), .in_6(rst), .out_7(ram_1_out_7), .out_8(ram_1_out_8));
  Pull_Resistor pull_resistor_1 (.node(pull_resistor_1_node));
  Pull_Resistor pull_resistor_2 (.node(pull_resistor_2_node));
  Pull_Resistor pull_resistor_3 (.node(ram_1_out_7));
  Pull_Resistor pull_resistor_4 (.node(pull_resistor_4_node));
  Pull_Resistor pull_resistor_5 (.node(pull_resistor_5_node));
  Pull_Resistor pull_resistor_6 (.node(ram_1_out_8));
  CPU cpu_1 (
    .in_1(rst), .in_2(CLK), .in_3(ram_1_out_8), .in_4(ram_1_out_7), .ABUS(pull_resistor_1_node),
    .DOUTBUS(pull_resistor_2_node), .out_8(pull_resistor_4_node), .out_9(pull_resistor_5_node),
    .inta(cpu_1_inta), .intr3__0(interrupt_interface_4_1_p1), .UEXT1__0(cpu_1_uext1__0));
  // INTERRUPT_INTERFACE_4 interrupt_interface_4_1: pin names not known; wires that end beside it: interrupt_interface_4_1_p1, cpu_1_inta, cpu_1_uext1__0, interrupt_interface_4_1_p4, interrupt_interface_4_1_p5, interrupt_interface_4_1_p6, interrupt_interface_4_1_p7, CLK
  Button BTN_INTR3 (.out(interrupt_interface_4_1_p4));
  Button BTN_INTR2 (.out(interrupt_interface_4_1_p5));
  Button BTN_INTR1 (.out(interrupt_interface_4_1_p6));
  Button BTN_INTR0 (.out(interrupt_interface_4_1_p7));
endmodule

module CPU (
  input  in_1,
  input  in_2,
  input  in_3,
  input  [7:0] in_4,
  input  [3:0] intr3__0,
  output [15:0] ABUS,
  output [7:0] DOUTBUS,
  output out_8,
  output out_9,
  output inta,
  output [1:0] UEXT1__0
);

  wire [3:0] common_1_phaseffbus;
  wire [7:0] A, common_1_addrbus, pull_resistor_5_node;
  wire [9:0] pull_resistor_2_node;
  wire [13:0] pull_resistor_6_node;
  wire [14:0] pull_resistor_4_node;
  wire [15:0] B, INTRADDR, PSW;
  wire [16:0] ALU;
  wire [21:0] common_1_instrucbus;

  COMMON common_1 (
    .CLK(in_2), .RST(in_1), .DIN(in_4), .CMEMBUS(pull_resistor_4_node), .MAR(ABUS), .MDR(DOUTBUS),
    .PHASEFFBUS(common_1_phaseffbus), .INSTRUCBUS(common_1_instrucbus), .ADDRBUS(common_1_addrbus),
    .CREGBUS(pull_resistor_6_node), .CFFBUS(pull_resistor_5_node), .B(B), .A(A), .CPSW(pull_resistor_2_node),
    .CALU(ALU), .IVTPPDSP(INTRADDR), .PSW(PSW));
  Pull_Resistor pull_resistor_1 (.node(common_1_instrucbus));
  Pull_Resistor pull_resistor_2 (.node(pull_resistor_2_node));
  Pull_Resistor pull_resistor_3 (.node(common_1_phaseffbus));
  Pull_Resistor pull_resistor_4 (.node(pull_resistor_4_node));
  Pull_Resistor pull_resistor_5 (.node(pull_resistor_5_node));
  Pull_Resistor pull_resistor_6 (.node(pull_resistor_6_node));
  Pull_Resistor pull_resistor_7 (.node(common_1_addrbus));
  FETCH fetch_1 (
    .in_1(in_1), .in_2(in_2), .in_3(in_3), .PHASEFFBUS(common_1_phaseffbus), .CMEMBUS(pull_resistor_4_node),
    .CFFBUS(pull_resistor_5_node), .INSTRUCBUS(common_1_instrucbus), .ADDRBUS(common_1_addrbus),
    .CREGBUS(pull_resistor_6_node), .PSW(PSW), .rdMEM(out_9));
  ADDR addr_1 (
    .in_1(in_1), .in_2(in_2), .in_3(in_3), .PHASEFFBUS(common_1_phaseffbus),
    .INSTRUCBUS(common_1_instrucbus), .ADDRBUS(common_1_addrbus), .rdMEM(out_9),
    .CMEMBUS(pull_resistor_4_node), .CFFBUS(pull_resistor_5_node), .CREGBUS(pull_resistor_6_node));
  // EXEC exec_1: pin names not known; wires that end beside it: common_1_phaseffbus, common_1_instrucbus, common_1_addrbus, pull_resistor_4_node, pull_resistor_5_node, pull_resistor_6_node, pull_resistor_2_node, in_1, in_2, B, PSW, A, ALU, out_8, out_9, in_3
  INTR intr_1 (
    .in_1(in_1), .in_2(in_2), .in_3(in_3), .PHASEFFBUS(common_1_phaseffbus),
    .INSTRUCBUS(common_1_instrucbus), .PSW(PSW), .intr(intr3__0), .ADDIVTP(INTRADDR),
    .CMEMBUS(pull_resistor_4_node), .CFFBUS(pull_resistor_5_node), .CREGBUS(pull_resistor_6_node),
    .rdMEM(out_9), .wrMEM(out_8), .UEXT1__0(UEXT1__0), .inta(inta));
  // Pins of 9 and 17 bits meet at ALU

  // Other names for the same wires on the sheet: CLK = in_2; DIN7__0[7:0] = in_4; FCBUS = in_3; MAR[15:0] = ABUS;
  //   MDR[7:0] = DOUTBUS; RD = out_9; rst = in_1; WR = out_8
endmodule

module COMMON (
  input  CLK,
  input  RST,
  input  [7:0] DIN,
  input  [7:0] A,
  input  [16:0] CALU,
  input  [15:0] IVTPPDSP,
  input  [14:0] CMEMBUS,
  input  [7:0] CFFBUS,
  input  [13:0] CREGBUS,
  input  [9:0] CPSW,
  output [15:0] MAR,
  output [7:0] MDR,
  output [3:0] PHASEFFBUS,
  output [21:0] INSTRUCBUS,
  output [7:0] ADDRBUS,
  output [15:0] PSW,
  output [15:0] B
);

  wire ADRINST, adrinst_t, and_1_out, and_2_out, and_6_out, and_9_out, and_10_out, and_11_out, and_12_out,
       and_13_out, and_14_out, and_15_out, and_16_out, and_17_out, and_18_out, and_19_out, and_20_out,
       and_21_out, and_22_out, and_23_out, and_24_out, and_25_out, and_26_out, and_27_out, and_28_out,
       bezadrinst, branchinst, C, jmpinst, mp2_16b_1_p3, mp4_8b_1_p5, mp4_8b_2_p5, mp4_16b_1_p5, mp8_8b_1_p8,
       mp8_16b_1_p8, N, not_2_out, not_4_out, not_5_out, not_6_out, not_7_out, not_8_out, not_10_out,
       not_11_out, not_12_out, not_13_out, not_15_out, not_16_out, or_1_out, or_2_out, or_4_out, or_5_out,
       or_6_out, or_7_out, or_8_out, or_9_out, or_10_out, or_11_out, or_12_out, or_13_out, or_14_out,
       or_15_out, reg8_inc_ld_1_p2, reg16_inc_ld_2_p4, regind, rsff_2_p4, rsff_3_p4, rsff_6_p4, V, Z;
  wire [3:0] IR27__24;
  wire [7:0] A15__8, DWH, DWL, IR7__0, IR15__8, IR23__16;
  wire [7:4] IR31__24;
  wire [15:0] ADDDEC15__0, ADDINC15__0, ADDIREG15__0, ADDPCREL15__0, GPR15__0, mp4_16b_2_p5, PC15__0, SP15__0;

  // MP4_8b mp4_8b_1: pin names not known; wires that end beside it: CREGBUS[2], CREGBUS[3], MDR, IR15__8, mp4_8b_1_p5, GPR15__0[15:8], CALU[15:8], 1'b1
  // REG8_INC_LD reg8_inc_ld_1: pin names not known; wires that end beside it: CLK, reg8_inc_ld_1_p2, mp4_8b_1_p5, B[15:8], CREGBUS[1]
  // ADD16 add16_1: pin names not known; wires that end beside it: {16{1'b1}}, ADDDEC15__0, GPR15__0, 1'b0
  // DC4_16 dc4_16_1: pin names not known; wires that end beside it: IR31__24, PSW[0], bezadrinst, branchinst, jmpinst, adrinst_t, INSTRUCBUS[20], INSTRUCBUS[20], INSTRUCBUS[20], INSTRUCBUS[20], INSTRUCBUS[20], INSTRUCBUS[20], INSTRUCBUS[20], INSTRUCBUS[20], INSTRUCBUS[20], INSTRUCBUS[20], INSTRUCBUS[20], INSTRUCBUS[20]
  // DC4_16 dc4_16_2: pin names not known; wires that end beside it: IR27__24, branchinst, INSTRUCBUS[7], INSTRUCBUS[8], INSTRUCBUS[9], INSTRUCBUS[10], INSTRUCBUS[11], INSTRUCBUS[20], INSTRUCBUS[20], INSTRUCBUS[20], INSTRUCBUS[20], INSTRUCBUS[20], INSTRUCBUS[20], INSTRUCBUS[20], INSTRUCBUS[20], INSTRUCBUS[20], INSTRUCBUS[20], INSTRUCBUS[20]
  // ADD16 add16_2: pin names not known; wires that end beside it: 16'h1, ADDINC15__0, GPR15__0, 1'b0
  and and_1 (and_1_out, ~CALU[7], B[7], A[7]);  // AND_Gate
  or or_1 (or_1_out, and_1_out, and_2_out);
  and and_2 (and_2_out, CALU[7], ~B[7], ~A[7]);  // AND_Gate
  // MP8_16b mp8_16b_1: pin names not known; wires that end beside it: CMEMBUS[9], CMEMBUS[10], CMEMBUS[11], PC15__0, {IR7__0, IR15__8}, ADDIREG15__0, SP15__0, mp8_16b_1_p8, IVTPPDSP, 1'b1
  // REG16_INC_LD reg16_inc_ld_1: pin names not known; wires that end beside it: CLK, mp8_16b_1_p8, MAR, CMEMBUS[0], CMEMBUS[1]
  // REG8_LD reg8_ld_1: pin names not known; wires that end beside it: CLK, MDR, {IR31__24, IR27__24}, CREGBUS[12]
  // REG8_LD reg8_ld_2: pin names not known; wires that end beside it: CLK, MDR, IR23__16, CREGBUS[11]
  not not_1 (reg8_inc_ld_1_p2, CREGBUS[13]);
  and and_3 (V, INSTRUCBUS[16], or_1_out);
  and and_4 (INSTRUCBUS[20], INSTRUCBUS[15], ADDRBUS[0]);
  // MP4_8b mp4_8b_2: pin names not known; wires that end beside it: CREGBUS[2], CREGBUS[3], MDR, IR7__0, mp4_8b_2_p5, GPR15__0[7:0], CALU[7:0], 1'b1
  // REG8_INC_LD reg8_inc_ld_2: pin names not known; wires that end beside it: CLK, reg8_inc_ld_1_p2, mp4_8b_2_p5, B[7:0], CREGBUS[0]
  // REG8_LD reg8_ld_3: pin names not known; wires that end beside it: CLK, MDR, IR15__8, CREGBUS[10]
  // REG8_LD reg8_ld_4: pin names not known; wires that end beside it: CLK, MDR, IR7__0, CREGBUS[9]
  // DC4_16 dc4_16_3: pin names not known; wires that end beside it: IR27__24, bezadrinst, INSTRUCBUS[0], INSTRUCBUS[1], INSTRUCBUS[2], INSTRUCBUS[3], INSTRUCBUS[4], INSTRUCBUS[5], INSTRUCBUS[6], INSTRUCBUS[20], INSTRUCBUS[20], INSTRUCBUS[20], INSTRUCBUS[20], INSTRUCBUS[20], INSTRUCBUS[20], INSTRUCBUS[20], INSTRUCBUS[20], INSTRUCBUS[20]
  // DC4_16 dc4_16_4: pin names not known; wires that end beside it: IR27__24, jmpinst, INSTRUCBUS[12], INSTRUCBUS[13], INSTRUCBUS[20], INSTRUCBUS[20], INSTRUCBUS[20], INSTRUCBUS[20], INSTRUCBUS[20], INSTRUCBUS[20], INSTRUCBUS[20], INSTRUCBUS[20], INSTRUCBUS[20], INSTRUCBUS[20], INSTRUCBUS[20], INSTRUCBUS[20], INSTRUCBUS[20], INSTRUCBUS[20]
  // ADD16 add16_3: pin names not known; wires that end beside it: {{9{IR23__16[7]}}, IR23__16[6:0]}, ADDPCREL15__0, PC15__0
  and and_5 (N, ADRINST, A[7]);
  // MP8_8b mp8_8b_1: pin names not known; wires that end beside it: CMEMBUS[12], CMEMBUS[13], CMEMBUS[14], DIN, A, PC15__0[15:8], PC15__0[7:0], mp8_8b_1_p8, {3'b000, PSW[4:0]}, {PSW[15], {7{1'b0}}}, A15__8, 1'b1
  // REG8_LD reg8_ld_5: pin names not known; wires that end beside it: CLK, mp8_8b_1_p8, MDR, CMEMBUS[2]
  // REG8_LD reg8_ld_6: pin names not known; wires that end beside it: CLK, MDR, DWH, CREGBUS[4]
  and and_6 (and_6_out, ~A[0], ~A[1], ~A[2], ~A[3], ~A[4], ~A[5], ~A[6], ~A[7]);  // AND_Gate
  // MP4_16b mp4_16b_1: pin names not known; wires that end beside it: CMEMBUS[5], CMEMBUS[6], {IR7__0, IR15__8}, ADDPCREL15__0, mp4_16b_1_p5, {DWH, DWL}, 1'b1
  // DC4_16 dc4_16_5: pin names not known; wires that end beside it: IR27__24, adrinst_t, INSTRUCBUS[14], INSTRUCBUS[15], INSTRUCBUS[16], INSTRUCBUS[17], INSTRUCBUS[18], INSTRUCBUS[19], INSTRUCBUS[20], INSTRUCBUS[20], INSTRUCBUS[20], INSTRUCBUS[20], INSTRUCBUS[20], INSTRUCBUS[20], INSTRUCBUS[20], INSTRUCBUS[20], INSTRUCBUS[20], INSTRUCBUS[20]
  // DC4_16 dc4_16_6: pin names not known; wires that end beside it: IR23__16[7:4], adrinst_t, ADDRBUS[0], ADDRBUS[1], ADDRBUS[2], regind, ADDRBUS[4], ADDRBUS[5], ADDRBUS[6], INSTRUCBUS[20], INSTRUCBUS[20], INSTRUCBUS[20], INSTRUCBUS[20], INSTRUCBUS[20], INSTRUCBUS[20], INSTRUCBUS[20], INSTRUCBUS[20], INSTRUCBUS[20]
  // REG16 reg16_1: pin names not known; wires that end beside it: CLK, 16'hf000, SP15__0, RST, CMEMBUS[7], CMEMBUS[8]
  and and_7 (Z, ADRINST, and_6_out);
  not not_2 (not_2_out, RST);
  // RSFF rsff_1: pin names not known; wires that end beside it: CFFBUS[1], CLK, CFFBUS[0], not_2_out, PHASEFFBUS[0]
  // MP2_16b mp2_16b_1: pin names not known; wires that end beside it: RST, mp4_16b_1_p5, mp2_16b_1_p3, 16'h1000, 1'b1
  // REG16_INC_LD reg16_inc_ld_2: pin names not known; wires that end beside it: CLK, mp2_16b_1_p3, PC15__0, reg16_inc_ld_2_p4, CMEMBUS[4]
  or or_2 (or_2_out, INSTRUCBUS[17], INSTRUCBUS[16]);
  or or_3 (reg16_inc_ld_2_p4, CMEMBUS[3], RST);
  // REG8_LD reg8_ld_7: pin names not known; wires that end beside it: CLK, MDR, DWL, CREGBUS[5]
  and and_8 (C, or_2_out, CALU[16]);
  // RSFF rsff_2: pin names not known; wires that end beside it: CFFBUS[3], CLK, CFFBUS[2], rsff_2_p4, PHASEFFBUS[1]
  not not_3 (rsff_2_p4, RST);
  not not_4 (not_4_out, C);
  not not_5 (not_5_out, V);
  not not_6 (not_6_out, N);
  and and_9 (and_9_out, CPSW[8], MDR[7]);
  and and_10 (and_10_out, CPSW[8], not_7_out);
  not not_7 (not_7_out, MDR[7]);
  and and_11 (and_11_out, CPSW[2], C);
  and and_12 (and_12_out, CPSW[2], not_4_out);
  and and_13 (and_13_out, CPSW[3], V);
  and and_14 (and_14_out, CPSW[3], not_5_out);
  and and_15 (and_15_out, CPSW[4], N);
  and and_16 (and_16_out, CPSW[4], not_6_out);
  and and_17 (and_17_out, CPSW[5], Z);
  and and_18 (and_18_out, CPSW[5], not_8_out);
  not not_8 (not_8_out, Z);
  // RSFF rsff_3: pin names not known; wires that end beside it: CFFBUS[5], CLK, CFFBUS[4], rsff_3_p4, PHASEFFBUS[2]
  not not_9 (rsff_3_p4, RST);
  or or_4 (or_4_out, CPSW[0], and_9_out);
  or or_5 (or_5_out, and_10_out, CPSW[1]);
  not not_10 (not_10_out, MDR[4]);
  not not_11 (not_11_out, MDR[3]);
  not not_12 (not_12_out, MDR[2]);
  and and_19 (and_19_out, CPSW[9], MDR[0]);
  and and_20 (and_20_out, CPSW[9], not_13_out);
  not not_13 (not_13_out, MDR[0]);
  // RSFF rsff_4: pin names not known; wires that end beside it: or_4_out, CLK, or_5_out, PSW[15]
  // NOT_Gate not_14 has open pins: in=RST, out=open
  and and_21 (and_21_out, CPSW[9], MDR[4]);
  and and_22 (and_22_out, CPSW[9], not_10_out);
  and and_23 (and_23_out, CPSW[9], MDR[3]);
  and and_24 (and_24_out, CPSW[9], not_11_out);
  and and_25 (and_25_out, CPSW[9], MDR[2]);
  and and_26 (and_26_out, CPSW[9], not_12_out);
  not not_15 (not_15_out, MDR[1]);
  or or_6 (or_6_out, CPSW[6], and_19_out);
  or or_7 (or_7_out, and_20_out, CPSW[7]);
  // MP4_16b mp4_16b_2: pin names not known; wires that end beside it: CREGBUS[7], CREGBUS[6], {A15__8, A}, ADDINC15__0, mp4_16b_2_p5, ADDDEC15__0
  GPR16x16 gpr16x16_1 (.CLK(CLK), .WR(CREGBUS[8]), .A3__0(IR23__16[3:0]), .Din15__0(mp4_16b_2_p5), .CLK_2(GPR15__0));
  or or_8 (or_8_out, and_11_out, and_21_out);
  or or_9 (or_9_out, and_22_out, and_12_out);
  or or_10 (or_10_out, and_13_out, and_23_out);
  or or_11 (or_11_out, and_24_out, and_14_out);
  or or_12 (or_12_out, and_15_out, and_25_out);
  or or_13 (or_13_out, and_26_out, and_16_out);
  or or_14 (or_14_out, and_17_out, and_27_out);
  and and_27 (and_27_out, CPSW[9], MDR[1]);
  and and_28 (and_28_out, CPSW[9], not_15_out);
  or or_15 (or_15_out, and_28_out, and_18_out);
  not not_16 (not_16_out, RST);
  // RSFF rsff_5: pin names not known; wires that end beside it: or_6_out, CLK, or_7_out, not_16_out, PSW[0]
  // RSFF rsff_6: pin names not known; wires that end beside it: CFFBUS[7], CLK, CFFBUS[6], rsff_6_p4, PHASEFFBUS[3]
  not not_17 (rsff_6_p4, RST);
  // RSFF rsff_7: pin names not known; wires that end beside it: or_8_out, CLK, or_9_out, PSW[4]
  // NOT_Gate not_18 has open pins: in=RST, out=open
  // RSFF rsff_8: pin names not known; wires that end beside it: or_10_out, CLK, or_11_out, PSW[3]
  // NOT_Gate not_19 has open pins: in=RST, out=open
  // RSFF rsff_9: pin names not known; wires that end beside it: or_12_out, CLK, or_13_out, PSW[2]
  // NOT_Gate not_20 has open pins: in=RST, out=open
  // RSFF rsff_10: pin names not known; wires that end beside it: or_14_out, CLK, or_15_out, PSW[1]
  // NOT_Gate not_21 has open pins: in=RST, out=open
  or or_16 (ADRINST, INSTRUCBUS[18], INSTRUCBUS[14], INSTRUCBUS[16], INSTRUCBUS[17], INSTRUCBUS[19]);

  assign ADDRBUS[3] = ADDRBUS[6];
  assign PSW[14:5] = {10{1'b0}};

  // Other names for the same wires on the sheet: A7__0[7:0] = A; immed = ADDRBUS[0]; memdir = ADDRBUS[1];
  //   memind = ADDRBUS[2]; postincr = ADDRBUS[4]; postdec = ADDRBUS[5]; regdir = ADDRBUS[6]; B7__0[7:0] = B[7:0];
  //   B15__8[7:0] = B[15:8]; ALU7__0[7:0] = CALU[7:0]; ALU7 = CALU[7]; ALU15__8[7:0] = CALU[15:8]; C8 = CALU[16];
  //   stFETCH = CFFBUS[0]; clFETCH = CFFBUS[1]; stADDR = CFFBUS[2]; clADDR = CFFBUS[3]; stEXEC = CFFBUS[4];
  //   clEXEC = CFFBUS[5]; stINTR = CFFBUS[6]; clINTR = CFFBUS[7]; ldMAR = CMEMBUS[0]; incMAR = CMEMBUS[1];
  //   ldMDR = CMEMBUS[2]; ldPC = CMEMBUS[3]; incPC = CMEMBUS[4]; mxPC1 = CMEMBUS[5]; mxPC0 = CMEMBUS[6];
  //   incSP = CMEMBUS[7]; decSP = CMEMBUS[8]; mxMAR2 = CMEMBUS[9]; mxMAR1 = CMEMBUS[10]; mxMAR0 = CMEMBUS[11];
  //   mxMDR2 = CMEMBUS[12]; mxMDR1 = CMEMBUS[13]; mxMDR0 = CMEMBUS[14]; stPSWI = CPSW[0]; clPSWI = CPSW[1];
  //   ldC = CPSW[2]; ldV = CPSW[3]; ldN = CPSW[4]; ldZ = CPSW[5]; clPSWSTART = CPSW[6]; stPSWSTART = CPSW[7];
  //   ldPSWH = CPSW[8]; ldPSWL = CPSW[9]; ldBL = CREGBUS[0]; ldBH = CREGBUS[1]; mxB1 = CREGBUS[2]; mxB0 = CREGBUS[3];
  //   ldDWH = CREGBUS[4]; ldDWL = CREGBUS[5]; mxGPR0 = CREGBUS[6]; mxGPR1 = CREGBUS[7]; wrGPR = CREGBUS[8];
  //   ldIR7__0 = CREGBUS[9]; ldIR15__8 = CREGBUS[10]; ldIR23__16 = CREGBUS[11]; ldIR31__24 = CREGBUS[12];
  //   clB = CREGBUS[13]; Din7__0[7:0] = DIN; ENTRADDR15__0[15:0] = IVTPPDSP; HALT = INSTRUCBUS[0];
  //   RTS = INSTRUCBUS[1]; RTI = INSTRUCBUS[2]; ROR = INSTRUCBUS[3]; RORC = INSTRUCBUS[4]; PUSH = INSTRUCBUS[5];
  //   POP = INSTRUCBUS[6]; BLEQ = INSTRUCBUS[7]; BGREU = INSTRUCBUS[8]; BNNG = INSTRUCBUS[9]; BGRT = INSTRUCBUS[10];
  //   JLEQ = INSTRUCBUS[11]; JMP = INSTRUCBUS[12]; JSR = INSTRUCBUS[13]; LD = INSTRUCBUS[14]; ST = INSTRUCBUS[15];
  //   ADD = INSTRUCBUS[16]; INC = INSTRUCBUS[17]; OR = INSTRUCBUS[18]; STRFIND = INSTRUCBUS[19];
  //   grinst = INSTRUCBUS[20]; IR31__24[3:0] = IR27__24; MAR15__0[15:0] = MAR; MDR7__0[7:0] = MDR;
  //   FETCH = PHASEFFBUS[0]; ADDR = PHASEFFBUS[1]; EXEC = PHASEFFBUS[2]; INTR = PHASEFFBUS[3];
  //   PSW7__0[4:0] = PSW[4:0]; PSWSTART = PSW[0]; PSWZ = PSW[1]; PSWN = PSW[2]; PSWV = PSW[3]; PSWC = PSW[4];
  //   PSW15__8[7] = PSW[15]; PSWI = PSW[15]

  // Notes on the sheet:
  //   Instrukcijski registar
  //   MAR
  //   Dekoderi za prepoznavanje instrukcije na osnovu sadrzaja registra IR23..16
  //   MDR
  //   PC
  //   FF za pokretanje FETCH, ADDR, EXEC i INTR faze izvršavanja instrukcije
  //   Programska statusna reč (PSW)
endmodule

module FETCH (
  input  in_1,
  input  in_2,
  input  in_3,
  input  [3:0] PHASEFFBUS,
  input  [21:0] INSTRUCBUS,
  input  [7:0] ADDRBUS,
  input  [15:0] PSW,
  output [14:0] CMEMBUS,
  output [7:0] CFFBUS,
  output [13:0] CREGBUS,
  output rdMEM
);

  wire addr2, addr4, addr_t, and_3_out, and_4_out, and_5_out, and_6_out, and_7_out, and_8_out, bezadr1,
       bradr2, brbezadr1, brcnd, brjmp2, brjmp3, brnotfcbus, bruncnd, clFETCH, incPC, jmp2, jmp3, ldIR7__0,
       ldIR15__8, ldIR23__16, ldIR31__24, ldMAR, ldMDR, not_1_out, not_3_out, not_4_out, not_5_out,
       notPSWSTandFETCH, or_6_out, or_7_out, rdMEM_t, reg5_cl_inc_ld_1_p5, reg5_cl_inc_ld_1_p6, stADDR,
       stEXEC;
  wire [4:0] reg5_cl_inc_ld_1_p3, reg5_cl_inc_ld_1_p4;
  wire [30:11] rom64x37_1_p3;

  or or_1 (bezadr1, INSTRUCBUS[0], INSTRUCBUS[1], INSTRUCBUS[2], INSTRUCBUS[3], INSTRUCBUS[4], INSTRUCBUS[5], INSTRUCBUS[6]);
  or or_2 (jmp3, INSTRUCBUS[11], INSTRUCBUS[12], INSTRUCBUS[13]);
  not not_1 (not_1_out, in_1);
  // REG5_CL_INC_LD reg5_cl_inc_ld_1: pin names not known; wires that end beside it: in_2, not_1_out, reg5_cl_inc_ld_1_p3, reg5_cl_inc_ld_1_p4, reg5_cl_inc_ld_1_p5, reg5_cl_inc_ld_1_p6
  // ROM64x37 rom64x37_1: pin names not known; wires that end beside it: {1'b0, reg5_cl_inc_ld_1_p4}, 1'b1, {rom64x37_1_p3[30:21], reg5_cl_inc_ld_1_p3, rom64x37_1_p3[15:11], stEXEC, stADDR, clFETCH, ldIR7__0, ldIR15__8, ldIR23__16, ldIR31__24, ldMDR, rdMEM_t, incPC, ldMAR}
  not not_2 (reg5_cl_inc_ld_1_p6, reg5_cl_inc_ld_1_p5);
  // DC4_16 dc4_16_1: pin names not known; wires that end beside it: rom64x37_1_p3[15:12], 1'b1, brjmp3, bruncnd, notPSWSTandFETCH, brbezadr1, brjmp2, bradr2, brnotfcbus
  or or_3 (jmp2, INSTRUCBUS[7], INSTRUCBUS[8], INSTRUCBUS[9], INSTRUCBUS[10]);
  or or_4 (reg5_cl_inc_ld_1_p5, bruncnd, brcnd);
  and and_1 (addr4, ADDRBUS[0], ADDRBUS[1], addr_t, ADDRBUS[2]);
  or or_5 (addr_t, INSTRUCBUS[17], INSTRUCBUS[14], INSTRUCBUS[15], INSTRUCBUS[16], INSTRUCBUS[18], INSTRUCBUS[19]);
  or or_6 (or_6_out, ADDRBUS[3], ADDRBUS[5], ADDRBUS[4], ADDRBUS[6]);
  and and_2 (addr2, addr_t, or_6_out);
  not not_3 (not_3_out, PHASEFFBUS[0]);
  not not_4 (not_4_out, PSW[0]);
  or or_7 (or_7_out, not_3_out, not_4_out);
  not not_5 (not_5_out, in_3);
  and and_3 (and_3_out, or_7_out, notPSWSTandFETCH);
  and and_4 (and_4_out, brbezadr1, bezadr1);
  and and_5 (and_5_out, brjmp2, jmp2);
  and and_6 (and_6_out, bradr2, addr2);
  and and_7 (and_7_out, brjmp3, jmp3);
  and and_8 (and_8_out, brnotfcbus, not_5_out);
  or or_8 (brcnd, and_3_out, and_4_out, and_5_out, and_6_out, and_7_out, and_8_out);
  assign CFFBUS[1] = clFETCH ? 1'b1 : 1'bz;  // Controlled_Buffer controlled_buffer_1
  assign CFFBUS[2] = stADDR ? 1'b1 : 1'bz;  // Controlled_Buffer controlled_buffer_2
  assign CFFBUS[4] = stEXEC ? 1'b1 : 1'bz;  // Controlled_Buffer controlled_buffer_3
  assign CREGBUS[9] = ldIR7__0 ? 1'b1 : 1'bz;  // Controlled_Buffer controlled_buffer_4
  assign CREGBUS[10] = ldIR15__8 ? 1'b1 : 1'bz;  // Controlled_Buffer controlled_buffer_5
  assign CREGBUS[11] = ldIR23__16 ? 1'b1 : 1'bz;  // Controlled_Buffer controlled_buffer_6
  assign CMEMBUS[0] = ldMAR ? 1'b1 : 1'bz;  // Controlled_Buffer controlled_buffer_7
  assign CMEMBUS[2] = ldMDR ? 1'b1 : 1'bz;  // Controlled_Buffer controlled_buffer_8
  assign CMEMBUS[4] = incPC ? 1'b1 : 1'bz;  // Controlled_Buffer controlled_buffer_9
  assign CREGBUS[12] = ldIR31__24 ? 1'b1 : 1'bz;  // Controlled_Buffer controlled_buffer_10
  assign rdMEM = rdMEM_t ? 1'b1 : 1'bz;  // Controlled_Buffer controlled_buffer_11

  // Other names for the same wires on the sheet: immed = ADDRBUS[0]; memdir = ADDRBUS[1]; memind = ADDRBUS[2];
  //   regind = ADDRBUS[3]; postincr = ADDRBUS[4]; postdec = ADDRBUS[5]; regdir = ADDRBUS[6]; CLK = in_2; FCBUS = in_3;
  //   HALT = INSTRUCBUS[0]; RTS = INSTRUCBUS[1]; RTI = INSTRUCBUS[2]; ROR = INSTRUCBUS[3]; RORC = INSTRUCBUS[4];
  //   PUSH = INSTRUCBUS[5]; POP = INSTRUCBUS[6]; BLEQ = INSTRUCBUS[7]; BGREU = INSTRUCBUS[8]; BNNG = INSTRUCBUS[9];
  //   BGRT = INSTRUCBUS[10]; JLEQ = INSTRUCBUS[11]; JMP = INSTRUCBUS[12]; JSR = INSTRUCBUS[13]; LD = INSTRUCBUS[14];
  //   ST = INSTRUCBUS[15]; ADD = INSTRUCBUS[16]; INC = INSTRUCBUS[17]; OR = INSTRUCBUS[18]; STRFIND = INSTRUCBUS[19];
  //   grinst = INSTRUCBUS[20]; FETCH = PHASEFFBUS[0]; ADDR = PHASEFFBUS[1]; EXEC = PHASEFFBUS[2];
  //   INTR = PHASEFFBUS[3]; PSWSTART = PSW[0]; rst = in_1

  // Notes on the sheet:
  //   Operaciona jedinica
  //   Kontrolna jedinica
endmodule

module ADDR (
  input  in_1,
  input  in_2,
  input  in_3,
  input  [3:0] PHASEFFBUS,
  input  [21:0] INSTRUCBUS,
  input  [7:0] ADDRBUS,
  output [14:0] CMEMBUS,
  output [7:0] CFFBUS,
  output [13:0] CREGBUS,
  output rdMEM
);


  // Other names for the same wires on the sheet: CLK = in_2; FCBUS = in_3; rst = in_1

  // Notes on the sheet:
  //   Operaciona jedinica
  //   Upravljacka jedinica
endmodule

module EXEC (
  input  in_1,
  input  in_2,
  input  in_3,
  input  [15:0] B,
  input  [3:0] PHASEFFBUS,
  input  [21:0] INSTRUCBUS,
  input  [7:0] ADDRBUS,
  input  [15:0] PSW,
  output [15:0] A,
  output [16:0] CALU,
  output [14:0] CMEMBUS,
  output [7:0] CFFBUS,
  output [13:0] CREGBUS,
  output [9:0] CPSW,
  output rdMEM,
  output wrMEM
);

  wire A7__0eqB7__0, addALU, and_1_out, and_2_out, and_3_out, and_4_out, and_5_out, and_6_out, and_7_out,
       brorjmp, C17, clPSWI, clPSWSTART, decSP, incALU, incMAR, incPC, incSP, ldAH, ldAL, ldC, ldMAR, ldMDR,
       ldN, ldPC, ldPSWH, ldPSWL, ldV, ldZ, mp2_1b_1_p3, mp4_8b_1_p5, mp4_8b_2_p5, mxA0, mxA1, mxALU0,
       mxMAR0, mxMAR1, mxMAR2, mxMDR0, mxMDR1, mxMDR2, mxPC0, mxPC1, mxROR, not_1_out, not_2_out, or_1_out,
       or_2_out, or_3_out, orALU, rdMEM_t, reg8_ld_sl_sr_2_p8, SRA, stPSWI, stPSWSTART, subALU, wrMEM_t,
       xor_1_out;
  wire [7:0] A15__8, MDR7__0;
  wire [15:0] ALU15__0, mp2_16b_1_p3;

  // MP2_1b mp2_1b_1: pin names not known; wires that end beside it: mxROR, A[0], mp2_1b_1_p3, PSW[4]
  // MP4_8b mp4_8b_1: pin names not known; wires that end beside it: mxA1, mxA0, ALU15__0[15:8], B[15:8], mp4_8b_1_p5, MDR7__0, 1'b1
  not not_1 (not_1_out, in_1);
  // REG8_LD_SL_SR reg8_ld_sl_sr_1: pin names not known; wires that end beside it: mp2_1b_1_p3, SRA, in_2, not_1_out, mp4_8b_1_p5, A15__8, ldAH
  // MP4_8b mp4_8b_2: pin names not known; wires that end beside it: mxA1, mxA0, ALU15__0[7:0], B[7:0], mp4_8b_2_p5, MDR7__0, 1'b1
  not not_2 (not_2_out, in_1);
  // REG8_LD_SL_SR reg8_ld_sl_sr_2: pin names not known; wires that end beside it: A15__8[0], SRA, in_2, not_2_out, mp4_8b_2_p5, A[7:0], ldAL, reg8_ld_sl_sr_2_p8
  ALU16_add_inc_or_sub alu16_add_inc_or_sub_1 (
    .A({A15__8, A[7:0]}), .A_2(ALU15__0), .B(mp2_16b_1_p3), .\or (orALU), .add(addALU), .inc(incALU),
    .C0(reg8_ld_sl_sr_2_p8), .sub(subALU), .c17(C17), .eq(A7__0eqB7__0));
  // MP2_16b mp2_16b_1: pin names not known; wires that end beside it: 1'b1, {{8{1'b0}}, MDR7__0}, mp2_16b_1_p3, B, mxALU0
  xor xor_1 (xor_1_out, PSW[2], PSW[3]);
  and and_1 (and_1_out, A7__0eqB7__0, INSTRUCBUS[19]);
  or or_1 (or_1_out, xor_1_out, PSW[1]);
  or or_2 (or_2_out, addALU, incALU, subALU);
  and and_2 (and_2_out, SRA, A[0]);
  and and_3 (and_3_out, INSTRUCBUS[10], ~or_1_out);  // AND_Gate
  and and_4 (and_4_out, or_1_out, or_3_out);
  or or_3 (or_3_out, INSTRUCBUS[11], INSTRUCBUS[7]);
  and and_5 (and_5_out, ~PSW[2], INSTRUCBUS[9]);  // AND_Gate
  and and_6 (and_6_out, ~PSW[4], INSTRUCBUS[8]);  // AND_Gate
  and and_7 (and_7_out, or_2_out, C17);
  or or_4 (CALU[16], and_7_out, and_2_out);
  or or_5 (brorjmp, and_3_out, and_4_out, and_1_out, and_5_out, and_6_out);
  assign CMEMBUS[7] = incSP ? 1'b1 : 1'bz;  // Controlled_Buffer controlled_buffer_1
  assign CMEMBUS[8] = decSP ? 1'b1 : 1'bz;  // Controlled_Buffer controlled_buffer_2
  assign CMEMBUS[9] = mxMAR2 ? 1'b1 : 1'bz;  // Controlled_Buffer controlled_buffer_3
  assign CPSW[0] = stPSWI ? 1'b1 : 1'bz;  // Controlled_Buffer controlled_buffer_4
  assign CPSW[1] = clPSWI ? 1'b1 : 1'bz;  // Controlled_Buffer controlled_buffer_5
  assign CPSW[2] = ldC ? 1'b1 : 1'bz;  // Controlled_Buffer controlled_buffer_6
  assign CPSW[3] = ldV ? 1'b1 : 1'bz;  // Controlled_Buffer controlled_buffer_7
  assign CPSW[4] = ldN ? 1'b1 : 1'bz;  // Controlled_Buffer controlled_buffer_8
  assign CPSW[5] = ldZ ? 1'b1 : 1'bz;  // Controlled_Buffer controlled_buffer_9
  assign CPSW[6] = clPSWSTART ? 1'b1 : 1'bz;  // Controlled_Buffer controlled_buffer_10
  assign CMEMBUS[5] = mxPC1 ? 1'b1 : 1'bz;  // Controlled_Buffer controlled_buffer_11
  assign CMEMBUS[6] = mxPC0 ? 1'b1 : 1'bz;  // Controlled_Buffer controlled_buffer_12
  assign CMEMBUS[12] = mxMDR2 ? 1'b1 : 1'bz;  // Controlled_Buffer controlled_buffer_13
  assign CMEMBUS[13] = mxMDR1 ? 1'b1 : 1'bz;  // Controlled_Buffer controlled_buffer_14
  assign CMEMBUS[14] = mxMDR0 ? 1'b1 : 1'bz;  // Controlled_Buffer controlled_buffer_15
  assign CMEMBUS[3] = ldPC ? 1'b1 : 1'bz;  // Controlled_Buffer controlled_buffer_16
  assign CMEMBUS[4] = incPC ? 1'b1 : 1'bz;  // Controlled_Buffer controlled_buffer_17
  assign CMEMBUS[10] = mxMAR1 ? 1'b1 : 1'bz;  // Controlled_Buffer controlled_buffer_18
  assign CMEMBUS[11] = mxMAR0 ? 1'b1 : 1'bz;  // Controlled_Buffer controlled_buffer_19
  assign CPSW[7] = stPSWSTART ? 1'b1 : 1'bz;  // Controlled_Buffer controlled_buffer_20
  assign CPSW[8] = ldPSWH ? 1'b1 : 1'bz;  // Controlled_Buffer controlled_buffer_21
  assign CMEMBUS[2] = ldMDR ? 1'b1 : 1'bz;  // Controlled_Buffer controlled_buffer_22
  assign CPSW[9] = ldPSWL ? 1'b1 : 1'bz;  // Controlled_Buffer controlled_buffer_23
  assign CMEMBUS[0] = ldMAR ? 1'b1 : 1'bz;  // Controlled_Buffer controlled_buffer_24
  assign CMEMBUS[1] = incMAR ? 1'b1 : 1'bz;  // Controlled_Buffer controlled_buffer_25
  assign rdMEM = rdMEM_t ? 1'b1 : 1'bz;  // Controlled_Buffer controlled_buffer_26
  assign wrMEM = wrMEM_t ? 1'b1 : 1'bz;  // Controlled_Buffer controlled_buffer_27

  assign CALU[7:0] = CALU[15:8];

  // Other names for the same wires on the sheet: B7__0[7:0] = B[7:0]; B15__8[7:0] = B[15:8]; A7__0[7:0] = A[7:0];
  //   A15__0[7:0] = A[15:8]; ALU7__0[7:0] = CALU[15:8]; C = CALU[16]; CLK = in_2; FCBUS = in_3; RTS = INSTRUCBUS[1];
  //   RTI = INSTRUCBUS[2]; ROR = INSTRUCBUS[3]; RORC = INSTRUCBUS[4]; PUSH = INSTRUCBUS[5]; POP = INSTRUCBUS[6];
  //   BLEQ = INSTRUCBUS[7]; BGREU = INSTRUCBUS[8]; BNNG = INSTRUCBUS[9]; BGRT = INSTRUCBUS[10]; JLEQ = INSTRUCBUS[11];
  //   JMP = INSTRUCBUS[12]; JSR = INSTRUCBUS[13]; LD = INSTRUCBUS[14]; ST = INSTRUCBUS[15]; ADD = INSTRUCBUS[16];
  //   INC = INSTRUCBUS[17]; OR = INSTRUCBUS[18]; STRFIND = INSTRUCBUS[19]; grinst = INSTRUCBUS[20];
  //   EXEC = PHASEFFBUS[2]; PSWSTART = PSW[0]; PSWZ = PSW[1]; PSWN = PSW[2]; PSWV = PSW[3]; PSWC = PSW[4];
  //   PSWI = PSW[15]; rst = in_1

  // Notes on the sheet:
  //   Operaciona jedinica
  //   Upravljacka jedinica
  //   Akumulator
  //   Ovo je samo kopirano treba prepraviti
endmodule

module INTR (
  input  in_1,
  input  in_2,
  input  in_3,
  input  [3:0] PHASEFFBUS,
  input  [21:0] INSTRUCBUS,
  input  [15:0] PSW,
  input  [3:0] intr,
  output [15:0] ADDIVTP,
  output [1:0] UEXT1__0,
  output inta,
  output [14:0] CMEMBUS,
  output [7:0] CFFBUS,
  output [13:0] CREGBUS,
  output rdMEM,
  output wrMEM
);


  // Other names for the same wires on the sheet: ADDIVTP15__0[15:0] = ADDIVTP; CLK = in_2; FCBUS = in_3;
  //   intr3__0[3:0] = intr; ldBR = inta; rst = in_1

  // Notes on the sheet:
  //   Operaciona jedinica
  //   Upravljacka jedinica
endmodule

module RAM (
  input  [15:0] in_1,
  input  in_2,
  input  [7:0] in_3,
  input  in_4,
  input  in_5,
  input  in_6,
  output [7:0] out_7,
  output out_8
);

  wire and_1_out, and_2_out, CNT0, LDCNT, not_1_out, notCNT0, or_1_out, reg4_ld_sl_sr_1_p6, rsff_2_p4,
       rsff_2_p5, rsff_3_p4, sl;
  wire [3:0] CNT, LFSR;

  // RSFF rsff_1: pin names not known; wires that end beside it: 1'b0, in_2, in_6, sl
  or or_1 (or_1_out, in_4, in_5);
  // REG4_LD_SL_SR reg4_ld_sl_sr_1: pin names not known; wires that end beside it: 1'b0, 1'b0, in_2, 4'b1111, LFSR, reg4_ld_sl_sr_1_p6, sl, in_6
  // RisingEdge risingedge_1: pin names not known; wires that end beside it: or_1_out, in_2, LDCNT
  // MEM64Kx8 mem64kx8_1: pin names not known; wires that end beside it: in_1, 1'b1, in_2, in_3, out_7, in_4
  xor xor_1 (reg4_ld_sl_sr_1_p6, LFSR[2], LFSR[3]);
  and and_1 (and_1_out, CNT0, not_1_out);
  not not_1 (not_1_out, LDCNT);
  // RSFF rsff_2: pin names not known; wires that end beside it: and_1_out, in_2, LDCNT, rsff_2_p4, rsff_2_p5
  not not_2 (rsff_2_p4, in_6);
  and and_2 (and_2_out, rsff_2_p5, CNT0);
  // REG4m_DEC_LD reg4m_dec_ld_1: pin names not known; wires that end beside it: in_2, LFSR, CNT, LDCNT, notCNT0, notCNT0
  or or_2 (notCNT0, CNT[0], CNT[1], CNT[2], CNT[3]);
  // RSFF rsff_3: pin names not known; wires that end beside it: out_8, in_2, and_2_out, rsff_3_p4, out_8
  not not_3 (rsff_3_p4, in_6);
  not not_4 (CNT0, notCNT0);

  // Other names for the same wires on the sheet: ADR[15:0] = in_1; CLK = in_2; DIN[7:0] = in_3; DOUT[7:0] = out_7;
  //   fc = out_8; RDMEM = in_5; rst = in_6; WRMEM = in_4

  // Notes on the sheet:
  //   Random broj predstavlja vreme pristupa memoriji
  //   Brojac za generisanje random broja 
  //   Jedinica za generisanje function complete (fc) signala
  //   Brojac za dekrementiranje random broja
endmodule
